// Logisim project dhbw_cpu.circ as structural Verilog
module Mainboard (
);

  CPU cpu_1 ();  // open: Out, Input, Interrupt, Takt
endmodule

module CPU (
  input  [7:0] Input,
  input  Interrupt,
  input  Takt,
  output [15:0] Out
);

  wire undriven;
  wire [7:0] register_1_flag_out, register_1_out_a, register_1_out_b, register_1_out_c, undriven_2,
       undriven_4;
  wire [19:0] undriven_3;

  RAM ram_1 ();  // open: Address_Low, Address_high, Data_In, Takt, Control_In, Output
  Register register_1 (
    .Takt(undriven), .Input(undriven_4), .Code(undriven_3), .Flag_In(undriven_2),
    .Flag_Out(register_1_flag_out), .Out_A(register_1_out_a), .Out_B(register_1_out_b),
    .Out_C(register_1_out_c), .Interrupt(Interrupt), .OID_Out(Out[15:8]));
  // ALU alu_1: pin names not known; wires that end beside it: Out[7:0]
endmodule

module ALU (
  input  [7:0] A_In,
  input  [7:0] B_In,
  input  [7:0] Flag_In,
  input  [4:0] Code,
  output [7:0] Flag_Out,
  output [7:0] Output
);

  wire adder_1_cout, adder_2_cout, bitfinder_1_found, comparator_1_eq, comparator_2_eq, comparator_2_lt,
       comparator_3_eq, pull_resistor_1_node, pull_resistor_2_node, pull_resistor_3_node, subtractor_1_bout,
       subtractor_2_bout;
  wire [6:0] adder_1_out, subtractor_1_out;
  wire [7:0] and_1_out, demultiplexer_1_out0, demultiplexer_1_out1, demultiplexer_1_out2,
       demultiplexer_1_out3, demultiplexer_1_out5, demultiplexer_1_out6, demultiplexer_1_out7,
       demultiplexer_2_out0, demultiplexer_2_out1, demultiplexer_2_out2, demultiplexer_2_out3,
       demultiplexer_2_out4, demultiplexer_2_out5, demultiplexer_2_out6, demultiplexer_2_out7,
       multiplexer_3_out, multiplier_1_cout, multiplier_1_out, not_1_out, or_2_out, pull_resistor_4_node,
       shifter_1_out, xor_1_out;
  wire [7:7] adder_2_out, subtractor_2_out;

  Comparator #(.width(3), .mode("unsigned")) comparator_1 (
    .a(3'b011), .b(Code[2:0]), .eq(comparator_1_eq));  // open: gt, lt
  Demultiplexer #(.select(3), .width(8), .disabled(0)) demultiplexer_1 (
    .out0(demultiplexer_1_out0), .out1(demultiplexer_1_out1), .out2(demultiplexer_1_out2),
    .out3(demultiplexer_1_out3), .out5(demultiplexer_1_out5), .out6(demultiplexer_1_out6),
    .out7(demultiplexer_1_out7), .in(B_In), .sel(Code[2:0]));  // open: out4, en
  Demultiplexer #(.select(3), .width(8), .disabled(0)) demultiplexer_2 (
    .out0(demultiplexer_2_out0), .out1(demultiplexer_2_out1), .out2(demultiplexer_2_out2),
    .out3(demultiplexer_2_out3), .out4(demultiplexer_2_out4), .out5(demultiplexer_2_out5),
    .out6(demultiplexer_2_out6), .out7(demultiplexer_2_out7), .in(A_In), .sel(Code[2:0]));  // open: en
  Pull_Resistor pull_resistor_1 (.node(pull_resistor_1_node));
  assign pull_resistor_1_node = Code[3] ? Flag_In[0] : 1'bz;  // Controlled_Buffer controlled_buffer_1
  or or_1 (Flag_Out[1], adder_1_cout, subtractor_1_bout);
  Adder #(.width(7)) adder_1 (
    .a(demultiplexer_2_out0[6:0]), .b(demultiplexer_1_out0[6:0]), .out(adder_1_out),
    .cin(pull_resistor_1_node), .cout(adder_1_cout));
  Adder #(.width(1)) adder_2 (
    .a(demultiplexer_2_out0[7]), .b(demultiplexer_1_out0[7]), .out(adder_2_out[7]), .cin(adder_1_cout),
    .cout(adder_2_cout));
  Pull_Resistor pull_resistor_2 (.node(pull_resistor_2_node));
  assign pull_resistor_2_node = Code[3] ? Flag_In[0] : 1'bz;  // Controlled_Buffer controlled_buffer_2
  Subtractor #(.width(7)) subtractor_1 (
    .a(demultiplexer_2_out1[6:0]), .b(demultiplexer_1_out1[6:0]), .out(subtractor_1_out),
    .bin(pull_resistor_2_node), .bout(subtractor_1_bout));
  Subtractor #(.width(1)) subtractor_2 (
    .a(demultiplexer_2_out1[7]), .b(demultiplexer_1_out1[7]), .out(subtractor_2_out[7]),
    .bin(subtractor_1_bout), .bout(subtractor_2_bout));
  Multiplier multiplier_1 (
    .a(demultiplexer_2_out2), .b(demultiplexer_1_out2), .out(multiplier_1_out), .cout(multiplier_1_cout));  // open: cin
  BitFinder bitfinder_1 (.in(multiplier_1_cout), .found(bitfinder_1_found));  // open: index
  Shifter #(.shift("lr")) shifter_1 (
    .in(demultiplexer_2_out2), .\dist (demultiplexer_1_out2[2:0]), .out(shifter_1_out));
  Comparator comparator_2 (
    .a(demultiplexer_2_out3), .b(demultiplexer_1_out3), .eq(comparator_2_eq), .lt(comparator_2_lt));  // open: gt
  assign not_1_out = ~demultiplexer_2_out4;  // NOT_Gate not_1, 8 bits wide
  assign or_2_out = demultiplexer_2_out5 | demultiplexer_1_out5;  // OR_Gate or_2, 8 bits wide
  assign and_1_out = demultiplexer_2_out6 & demultiplexer_1_out6;  // AND_Gate and_1, 8 bits wide
  assign xor_1_out = demultiplexer_2_out7 ^ demultiplexer_1_out7;  // XOR_Gate xor_1, 8 bits wide
  Multiplexer #(.disabled(0)) multiplexer_1 (
    .in0(comparator_3_eq), .in1(comparator_2_eq), .out(Flag_Out[4]), .sel(comparator_1_eq));  // open: en
  or or_3 (Flag_Out[0], adder_2_cout, subtractor_2_bout, pull_resistor_3_node, comparator_2_lt);
  Pull_Resistor pull_resistor_3 (.node(pull_resistor_3_node));
  assign pull_resistor_3_node = Code[4] ? bitfinder_1_found : 1'bz;  // Controlled_Buffer controlled_buffer_3
  Comparator #(.mode("unsigned")) comparator_3 (
    .a({8{1'b0}}), .b({Flag_Out[2], Output[6:1], Flag_Out[3]}), .eq(comparator_3_eq));  // open: gt, lt
  Multiplexer #(.select(3), .width(8), .disabled(0)) multiplexer_2 (
    .in0({adder_2_out[7], adder_1_out}), .in1({subtractor_2_out[7], subtractor_1_out}),
    .in2(multiplexer_3_out), .in3(pull_resistor_4_node), .in4(not_1_out), .in5(or_2_out), .in6(and_1_out),
    .in7(xor_1_out), .out({Flag_Out[2], Output[6:1], Flag_Out[3]}), .sel(Code[2:0]));  // open: en
  Pull_Resistor pull_resistor_4 (.node(pull_resistor_4_node));
  Multiplexer #(.width(8), .disabled(0)) multiplexer_3 (
    .in0(multiplier_1_out), .in1(shifter_1_out), .out(multiplexer_3_out), .sel(Code[4]));  // open: en

  assign Flag_Out[7:5] = Flag_In[7:5];
  assign {Output[7], Output[0]} = {Flag_Out[2], Flag_Out[3]};
endmodule

module RAM (
  input  [7:0] Address_Low,
  input  [7:0] Address_high,
  input  [7:0] Data_In,
  input  Takt,
  input  [1:0] Control_In,
  output [7:0] Output
);

  wire or_1_out;

  or or_1 (or_1_out, Control_In[0], Control_In[1]);
  RAM_part #(.addrWidth(16), .bus("separate")) ram_1 (
    .addr({Address_high, Address_Low}), .din(Data_In), .data(Output), .str(Control_In[0]), .sel(or_1_out),
    .clk(Takt), .ld(Control_In[1]));  // open: clr
  Pull_Resistor pull_resistor_1 (.node(Output));
endmodule

module Register (
  input  Takt,
  input  [7:0] Input,
  input  [19:0] Code,
  input  [7:0] Flag_In,
  input  Interrupt,
  output [7:0] Out_A,
  output [7:0] Out_B,
  output [7:0] Out_C,
  output [7:0] OID_Out,
  output [7:0] Flag_Out
);

  wire decoder_1_out1, decoder_1_out2, decoder_1_out3, decoder_1_out4, decoder_1_out5, decoder_1_out6,
       decoder_1_out7, decoder_1_out8, decoder_1_out9, decoder_1_out10, decoder_1_out11, decoder_1_out12,
       decoder_1_out13, decoder_1_out14, decoder_1_out15, not_1_out, or_3_out, pull_resistor_1_node,
       pull_resistor_4_node;
  wire [5:5] or_1_out;
  wire [7:0] AX_q, BX_q, controlled_buffer_1_out, CX_q, DPH_q, DX_q, EX_q, FX_q, GX_q, HX_q, IPH_q, IPL_q,
       or_2_out, pull_resistor_3_node, pull_resistor_5_node, pull_resistor_6_node, pull_resistor_7_node,
       SPH_q, SPL_q;

  not not_1 (not_1_out, Code[18]);
  Decoder #(.select(4), .disabled(0)) decoder_1 (
    .out1(decoder_1_out1), .out2(decoder_1_out2), .out3(decoder_1_out3), .out4(decoder_1_out4),
    .out5(decoder_1_out5), .out6(decoder_1_out6), .out7(decoder_1_out7), .out8(decoder_1_out8),
    .out9(decoder_1_out9), .out10(decoder_1_out10), .out11(decoder_1_out11), .out12(decoder_1_out12),
    .out13(decoder_1_out13), .out14(decoder_1_out14), .out15(decoder_1_out15), .sel(Code[3:0]));  // open: out0, en
  Pull_Resistor pull_resistor_1 (.node(pull_resistor_1_node));
  assign controlled_buffer_1_out = Code[16] ? {Flag_In[7:6], or_1_out[5], Flag_In[4:0]} : 8'bz;  // Controlled_Buffer controlled_buffer_1
  assign pull_resistor_1_node = not_1_out ? Flag_In[5] : 1'bz;  // Controlled_Buffer controlled_buffer_2
  Pull_Resistor pull_resistor_2 (.node(controlled_buffer_1_out));
  or or_1 (or_1_out[5], pull_resistor_1_node, Interrupt);
  Pull_Resistor pull_resistor_3 (.node(pull_resistor_3_node));
  assign pull_resistor_3_node = Code[16] ? Input : 8'bz;  // Controlled_Buffer controlled_buffer_3
  Pull_Resistor pull_resistor_4 (.node(pull_resistor_4_node));
  assign pull_resistor_4_node = Code[16] ? decoder_1_out15 : 1'bz;  // Controlled_Buffer controlled_buffer_4
  assign or_2_out = pull_resistor_3_node | controlled_buffer_1_out;  // OR_Gate or_2, 8 bits wide
  or or_3 (or_3_out, pull_resistor_4_node, Code[17]);
  Pull_Resistor pull_resistor_5 (.node(pull_resistor_5_node));
  Register_part #(.trigger("falling")) AX (.D(Input), .en(decoder_1_out1), .Q(AX_q), .clk(Takt));  // open: clr
  Register_part #(.trigger("falling")) BX (.D(Input), .en(decoder_1_out2), .Q(BX_q), .clk(Takt));  // open: clr
  Register_part #(.trigger("falling")) CX (.D(Input), .en(decoder_1_out3), .Q(CX_q), .clk(Takt));  // open: clr
  Register_part #(.trigger("falling")) DX (.D(Input), .en(decoder_1_out4), .Q(DX_q), .clk(Takt));  // open: clr
  Register_part #(.trigger("falling")) EX (.D(Input), .en(decoder_1_out5), .Q(EX_q), .clk(Takt));  // open: clr
  Register_part #(.trigger("falling")) FX (.D(Input), .en(decoder_1_out6), .Q(FX_q), .clk(Takt));  // open: clr
  Register_part #(.trigger("falling")) GX (.D(Input), .en(decoder_1_out7), .Q(GX_q), .clk(Takt));  // open: clr
  Register_part #(.trigger("falling")) HX (.D(Input), .en(decoder_1_out8), .Q(HX_q), .clk(Takt));  // open: clr
  Register_part #(.trigger("falling")) DPH (.D(Input), .en(decoder_1_out9), .Q(DPH_q), .clk(Takt));  // open: clr
  Register_part #(.trigger("falling")) SPL (.D(Input), .en(decoder_1_out10), .Q(SPL_q), .clk(Takt));  // open: clr
  Register_part #(.trigger("falling")) SPH (.D(Input), .en(decoder_1_out11), .Q(SPH_q), .clk(Takt));  // open: clr
  Register_part #(.trigger("falling")) IPL (.D(Input), .en(decoder_1_out12), .Q(IPL_q), .clk(Takt));  // open: clr
  Register_part #(.trigger("falling")) IPH (.D(Input), .en(decoder_1_out13), .Q(IPH_q), .clk(Takt));  // open: clr
  Register_part #(.trigger("falling")) OID (.D(Input), .en(decoder_1_out14), .Q(OID_Out), .clk(Takt));  // open: clr
  Register_part #(.trigger("falling")) Flag (.D(or_2_out), .en(or_3_out), .Q(Flag_Out), .clk(Takt));  // open: clr
  Multiplexer #(.select(4), .width(8), .disabled(0)) multiplexer_1 (
    .in0(pull_resistor_5_node), .in1(AX_q), .in2(BX_q), .in3(CX_q), .in4(DX_q), .in5(EX_q), .in6(FX_q),
    .in7(GX_q), .in8(HX_q), .in9(DPH_q), .in10(SPL_q), .in11(SPH_q), .in12(IPL_q), .in13(IPH_q),
    .in14(OID_Out), .in15(Flag_Out), .out(Out_A), .sel(Code[7:4]));  // open: en
  Pull_Resistor pull_resistor_6 (.node(pull_resistor_6_node));
  Multiplexer #(.select(4), .width(8), .disabled(0)) multiplexer_2 (
    .in0(pull_resistor_6_node), .in1(AX_q), .in2(BX_q), .in3(CX_q), .in4(DX_q), .in5(EX_q), .in6(FX_q),
    .in7(GX_q), .in8(HX_q), .in9(DPH_q), .in10(SPL_q), .in11(SPH_q), .in12(IPL_q), .in13(IPH_q),
    .in14(OID_Out), .in15(Flag_Out), .out(Out_B), .sel(Code[11:8]));  // open: en
  Pull_Resistor pull_resistor_7 (.node(pull_resistor_7_node));
  Multiplexer #(.select(4), .width(8), .disabled(0)) multiplexer_3 (
    .in0(pull_resistor_7_node), .in1(AX_q), .in2(BX_q), .in3(CX_q), .in4(DX_q), .in5(EX_q), .in6(FX_q),
    .in7(GX_q), .in8(HX_q), .in9(DPH_q), .in10(SPL_q), .in11(SPH_q), .in12(IPL_q), .in13(IPH_q),
    .in14(OID_Out), .in15(Flag_Out), .out(Out_C), .sel(Code[15:12]));  // open: en
endmodule
